// Digital circuit ALU_Arch.dig as structural Verilog
module ALU_Arch (
  input  B0,
  input  B1,
  input  B2,
  input  B3,
  input  B4,
  input  B5,
  input  B6,
  input  B7,
  input  C0,
  input  C1,
  input  A0,
  input  A1,
  input  A4,
  input  A5,
  input  A3,
  input  A2,
  input  A7,
  input  A6,
  output C2,
  output S3,
  output C3,
  output S7,
  output S6,
  output S4,
  output S1,
  output S0,
  output S5,
  output S2
);

  _74283 _74283_1 (
    .pin1(S5), .pin2(B5), .pin3(A5), .pin4(S4), .pin5(A4), .pin6(B4), .pin7(C1), .pin8(1'b0), .pin9(C3),
    .pin10(S7), .pin11(B7), .pin12(A7), .pin13(S6), .pin14(A6), .pin15(B6), .pin16(1'b1));
  _74283 _74283_2 (
    .pin1(S1), .pin2(B1), .pin3(A1), .pin4(S0), .pin5(A0), .pin6(B0), .pin7(C0), .pin8(1'b0), .pin9(C2),
    .pin10(S3), .pin11(B3), .pin12(A3), .pin13(S2), .pin14(A2), .pin15(B2), .pin16(1'b1));

  // Notes on the sheet:
  //   B0: pin 28
  //   B1: pin 27
  //   B2: pin 26
  //   B3: pin 25
  //   B4: pin 24
  //   B5: pin 23
  //   B6: pin 22
  //   B7: pin 21
  //   C0: pin 20
  //   C1: pin 9
  //   A0: pin 8
  //   A1: pin 7
  //   A4: pin 4
  //   A5: pin 3
  //   A3: pin 5
  //   A2: pin 6
  //   A7: pin 1
  //   A6: pin 2
  //   C2: pin 10
  //   S3: pin 14
  //   C3: pin 19
  //   S7: pin 18
  //   S6: pin 17
  //   S4: pin 15
  //   S1: pin 12
  //   S0: pin 11
  //   S5: pin 16
  //   S2: pin 13
endmodule
