// Digital circuit Arch_RAM.dig as structural Verilog
module Arch_RAM (
  input  A0,
  input  A1,
  input  A2,
  input  A3,
  input  EN,
  output Q0,
  output Q1,
  output Q2,
  output Q3,
  output Q4,
  output Q5,
  output Q6,
  output Q7
);

  ROM #(.AddrBits(4), .Bits(8)) rom_1 (.A({A3, A2, A1, A0}), .sel(EN), .D({Q7, Q6, Q5, Q4, Q3, Q2, Q1, Q0}));

  // Notes on the sheet:
  //   contents of rom_1 (hex, n*v repeats v):
  //   1f,2e,30,80,10*0,12,5
endmodule
