// Digital circuit Arch_ROM.dig as structural Verilog
module Arch_ROM (
  input  S0,
  input  S1,
  input  S2,
  input  I0,
  input  I1,
  input  I2,
  input  I3,
  input  EN,
  output HLT,
  output MI,
  output RI,
  output RO,
  output II,
  output IO,
  output AI,
  output AO,
  output \Σ0 ,
  output \ΣS ,
  output BI,
  output OI,
  output CE,
  output CO,
  output J,
  output WE
);

  ROM #(.AddrBits(7), .Bits(16)) rom_1 (
    .A({I3, I2, I1, I0, S2, S1, S0}), .sel(EN),
    .D({J, CO, CE, OI, BI, \ΣS , \Σ0 , AO, AI, IO, II, RO, WE, RI, MI, HLT}));
endmodule
