// Digital circuit BE_CPU_BUILD.dig as structural Verilog
module BE_CPU_BUILD (
  input  clk,
  input  _1,
  input  _2,
  input  _4,
  input  _8,
  input  _16,
  input  _32,
  input  _64,
  input  _128,
  input  in_10,
  input  A0,
  input  A1,
  input  A2,
  input  A3,
  input  in_15,
  input  HLT,
  input  MI,
  input  MO,
  input  BI,
  input  \ΣO ,
  input  AI,
  input  AO,
  input  \ΣS ,
  input  J,
  input  CO,
  input  CE,
  input  II,
  input  IO,
  input  OI,
  input  Manual_Mode,
  input  Manual_Control
);

  wire _74138_1_pin1, _74138_1_pin2, _74138_1_pin3, _74138_1_pin10, _74138_1_pin11, _74138_1_pin12,
       _74138_1_pin13, _74138_1_pin14, _74138_1_pin15, _74161_2_pin1, _74161_2_pin3, _74161_2_pin4,
       _74161_2_pin5, _74161_2_pin6, _74161_2_pin9, _74161_2_pin15, _74173_1_pin3, _74173_1_pin4,
       _74173_1_pin5, _74173_1_pin6, _74173_1_pin7, _74173_1_pin9, _74173_1_pin11, _74173_1_pin12,
       _74173_1_pin13, _74173_1_pin14, _74173_2_pin3, _74173_2_pin4, _74173_2_pin5, _74173_2_pin6,
       _74173_2_pin11, _74173_2_pin12, _74173_2_pin13, _74173_2_pin14, _74173_3_pin3, _74173_3_pin4,
       _74173_3_pin5, _74173_3_pin6, _74173_3_pin9, _74173_5_pin3, _74173_5_pin4, _74173_5_pin5,
       _74173_5_pin6, _74173_5_pin15, _74173_6_pin15, _74173_7_pin3, _74173_7_pin4, _74173_7_pin5,
       _74173_7_pin6, _74173_9_pin15, alu_arch_1_c2, arch_ram_1_q0, arch_ram_1_q1, arch_ram_1_q2,
       arch_ram_1_q3, arch_ram_1_q4, arch_ram_1_q5, arch_ram_1_q6, arch_ram_1_q7, bin_dec_hund_decoder_1_a,
       bin_dec_hund_decoder_1_b, bin_dec_hund_decoder_1_c, bin_dec_hund_decoder_1_d,
       bin_dec_hund_decoder_1_e, bin_dec_hund_decoder_1_f, bin_dec_hund_decoder_1_g,
       bin_dec_ones_decoder_1_a, bin_dec_ones_decoder_1_b, bin_dec_ones_decoder_1_c,
       bin_dec_ones_decoder_1_d, bin_dec_ones_decoder_1_e, bin_dec_ones_decoder_1_f,
       bin_dec_ones_decoder_1_g, bin_dec_tens_decoder_1_a, bin_dec_tens_decoder_1_b,
       bin_dec_tens_decoder_1_c, bin_dec_tens_decoder_1_d, bin_dec_tens_decoder_1_e,
       bin_dec_tens_decoder_1_f, bin_dec_tens_decoder_1_g, Clear_2_out, Clear_4_out, Clear_out,
       control_rom_1_ai, control_rom_1_ao, control_rom_1_bi, control_rom_1_ce, control_rom_1_co,
       control_rom_1_hlt, control_rom_1_ii, control_rom_1_io, control_rom_1_j, control_rom_1_mi,
       control_rom_1_mo, control_rom_1_oi, \control_rom_1_σo , \control_rom_1_σs , driver_1_out,
       driver_2_out, driver_3_out, driver_4_out, not_1_out, not_2_out, not_3_out, not_4_out, not_5_out,
       not_6_out, not_7_out, not_11_out, not_14_out, not_15_out, not_16_out, or_1_out, or_2_out, or_3_out,
       or_4_out, or_5_out, or_6_out, or_7_out, or_8_out, or_9_out, or_10_out, or_11_out, or_12_out,
       or_13_out, or_14_out, P_out, subtractor_chip_1_c0, subtractor_chip_1_q0, subtractor_chip_1_q1,
       subtractor_chip_1_q2, subtractor_chip_1_q3, subtractor_chip_1_q4, subtractor_chip_1_q5,
       subtractor_chip_1_q6, subtractor_chip_1_q7, switchdt_1_p3, tri_state_buffer_1_p2,
       tri_state_buffer_1_p3, tri_state_buffer_1_p5, tri_state_buffer_1_p7, tri_state_buffer_1_p9,
       tri_state_buffer_1_p11, tri_state_buffer_1_p12, tri_state_buffer_1_p13, tri_state_buffer_1_p14,
       tri_state_buffer_1_p15, tri_state_buffer_1_p16, tri_state_buffer_1_p17, tri_state_buffer_1_p18,
       tri_state_buffer_2_p2, tri_state_buffer_2_p4, tri_state_buffer_2_p6, tri_state_buffer_2_p8,
       tri_state_buffer_2_p10, tri_state_buffer_3_p2, tri_state_buffer_6_p4, tri_state_buffer_6_p6,
       tri_state_buffer_6_p8, tri_state_buffer_6_p10, tri_state_buffer_6_p12, tri_state_buffer_6_p14,
       tri_state_buffer_6_p16, tri_state_buffer_6_p18, tri_state_buffer_7_p12, tri_state_buffer_7_p13,
       tri_state_buffer_7_p14, tri_state_buffer_7_p15, tri_state_buffer_8_p12, tri_state_buffer_8_p13,
       tri_state_buffer_8_p14, tri_state_buffer_8_p15, tri_state_buffer_8_p16, tri_state_buffer_8_p17,
       tri_state_buffer_8_p18, tri_state_buffer_8_p19, tri_state_buffer_9_p12, tri_state_buffer_9_p13,
       tri_state_buffer_9_p14, tri_state_buffer_9_p15, tri_state_buffer_9_p16, tri_state_buffer_9_p17,
       tri_state_buffer_9_p18, tri_state_buffer_9_p19, tri_state_buffer_10_p12, tri_state_buffer_10_p13,
       tri_state_buffer_10_p14, tri_state_buffer_10_p15, tri_state_buffer_10_p16, tri_state_buffer_10_p17,
       tri_state_buffer_10_p18, tri_state_buffer_10_p19, tri_state_buffer_12_p11, tri_state_buffer_12_p12,
       tri_state_buffer_12_p13, tri_state_buffer_12_p14, tri_state_buffer_12_p15, tri_state_buffer_12_p16,
       tri_state_buffer_12_p17, tri_state_buffer_12_p18, tri_state_buffer_13_p11, tri_state_buffer_13_p12,
       tri_state_buffer_13_p13, tri_state_buffer_13_p14, tri_state_buffer_13_p15, tri_state_buffer_13_p16,
       tri_state_buffer_13_p17, tri_state_buffer_13_p18;

  not not_1 (not_1_out, Manual_Control);
  not not_2 (not_2_out, _74173_1_pin7);
  _74138 _74138_1 (
    .pin1(_74138_1_pin1), .pin2(_74138_1_pin2), .pin3(_74138_1_pin3), .pin4(1'b0), .pin5(1'b0), .pin6(1'b1),
    .pin8(1'b0), .pin10(_74138_1_pin10), .pin11(_74138_1_pin11), .pin12(_74138_1_pin12),
    .pin13(_74138_1_pin13), .pin14(_74138_1_pin14), .pin15(_74138_1_pin15), .pin16(1'b1));  // open: pin7, pin9
  _74161 _74161_1 (
    .pin1(_74138_1_pin10), .pin2(not_2_out), .pin3(1'b0), .pin4(1'b0), .pin5(1'b0), .pin6(1'b0), .pin7(1'b1),
    .pin8(1'b0), .pin9(1'b1), .pin10(1'b1), .pin12(_74138_1_pin3), .pin13(_74138_1_pin2),
    .pin14(_74138_1_pin1), .pin16(1'b1));  // open: pin11, pin15
  LED led_1 (.in(not_3_out));
  LED led_2 (.in(not_4_out));
  not not_3 (not_3_out, _74138_1_pin15);
  not not_4 (not_4_out, _74138_1_pin14);
  LED led_3 (.in(not_5_out));
  LED led_4 (.in(not_6_out));
  not not_5 (not_5_out, _74138_1_pin13);
  not not_6 (not_6_out, _74138_1_pin12);
  Button Clear (.out(Clear_out));
  LED led_5 (.in(not_7_out));
  not not_7 (not_7_out, _74138_1_pin11);
  _74173 _74173_1 (
    .pin1(1'b0), .pin2(1'b0), .pin3(_74173_1_pin3), .pin4(_74173_1_pin4), .pin5(_74173_1_pin5),
    .pin6(_74173_1_pin6), .pin7(_74173_1_pin7), .pin8(1'b0), .pin9(_74173_1_pin9), .pin10(_74173_1_pin9),
    .pin11(_74173_1_pin11), .pin12(_74173_1_pin12), .pin13(_74173_1_pin13), .pin14(_74173_1_pin14),
    .pin15(Clear_out), .pin16(1'b1));
  assign driver_1_out = in_15 ? A0 : 1'bz;  // Driver driver_1
  assign driver_2_out = in_15 ? A1 : 1'bz;  // Driver driver_2
  assign driver_3_out = in_15 ? A2 : 1'bz;  // Driver driver_3
  assign driver_4_out = in_15 ? A3 : 1'bz;  // Driver driver_4
  Control_Rom control_rom_1 (
    .S0(_74138_1_pin1), .S1(_74138_1_pin2), .S2(_74138_1_pin3), .I0(_74173_2_pin3), .I1(_74173_2_pin4),
    .I2(_74173_2_pin5), .I3(_74173_2_pin6), .EN(not_1_out), .J(control_rom_1_j), .CO(control_rom_1_co),
    .CE(control_rom_1_ce), .OI(control_rom_1_oi), .BI(control_rom_1_bi), .\ΣS (\control_rom_1_σs ),
    .\ΣO (\control_rom_1_σo ), .AO(control_rom_1_ao), .AI(control_rom_1_ai), .IO(control_rom_1_io),
    .II(control_rom_1_ii), .MO(control_rom_1_mo), .MI(control_rom_1_mi), .HLT(control_rom_1_hlt));
  _74173 _74173_2 (
    .pin1(1'b0), .pin2(1'b0), .pin3(_74173_2_pin3), .pin4(_74173_2_pin4), .pin5(_74173_2_pin5),
    .pin6(_74173_2_pin6), .pin7(not_2_out), .pin8(1'b0), .pin9(_74138_1_pin11), .pin10(_74138_1_pin11),
    .pin11(_74173_2_pin11), .pin12(_74173_2_pin12), .pin13(_74173_2_pin13), .pin14(_74173_2_pin14),
    .pin15(1'b0), .pin16(1'b1));
  // Tri_State_Buffer tri_state_buffer_1: pin names not known; wires that end beside it: 1'b0, tri_state_buffer_1_p2, tri_state_buffer_1_p3, _74173_1_pin14, tri_state_buffer_1_p5, _74173_1_pin13, tri_state_buffer_1_p7, _74173_1_pin12, tri_state_buffer_1_p9, _74173_1_pin11, tri_state_buffer_1_p11, tri_state_buffer_1_p12, tri_state_buffer_1_p13, tri_state_buffer_1_p14, tri_state_buffer_1_p15, tri_state_buffer_1_p16, tri_state_buffer_1_p17, tri_state_buffer_1_p18, 1'b1
  not not_8 (tri_state_buffer_1_p2, _74173_1_pin9);
  LED led_6 (.in(_74173_1_pin3));
  LED u_A0 (.in(driver_1_out));
  LED u_A1 (.in(driver_2_out));
  LED led_7 (.in(_74173_1_pin4));
  LED led_8 (.in(_74173_1_pin5));
  Button Clear_2 (.out(Clear_2_out));
  LED u_A2 (.in(driver_3_out));
  LED u_A3 (.in(driver_4_out));
  LED led_9 (.in(_74173_1_pin6));
  LED led_10 (.in(_74173_2_pin14));
  // Tri_State_Buffer tri_state_buffer_2: pin names not known; wires that end beside it: 1'b0, tri_state_buffer_2_p2, tri_state_buffer_1_p3, tri_state_buffer_2_p4, tri_state_buffer_1_p5, tri_state_buffer_2_p6, tri_state_buffer_1_p7, tri_state_buffer_2_p8, tri_state_buffer_1_p9, tri_state_buffer_2_p10, 1'b0, 1'b0, 1'b0, 1'b0, 1'b0, 1'b0, 1'b0, 1'b0, 1'b1
  _74173 _74173_3 (
    .pin1(1'b0), .pin2(1'b0), .pin3(_74173_3_pin3), .pin4(_74173_3_pin4), .pin5(_74173_3_pin5),
    .pin6(_74173_3_pin6), .pin7(_74173_1_pin7), .pin8(1'b0), .pin9(_74173_3_pin9), .pin10(_74173_3_pin9),
    .pin11(tri_state_buffer_2_p10), .pin12(tri_state_buffer_2_p8), .pin13(tri_state_buffer_2_p6),
    .pin14(tri_state_buffer_2_p4), .pin15(Clear_2_out), .pin16(1'b1));
  // Tri_State_Buffer tri_state_buffer_3: pin names not known; wires that end beside it: 1'b0, tri_state_buffer_3_p2, _74173_3_pin3, driver_1_out, _74173_3_pin4, driver_2_out, _74173_3_pin5, driver_3_out, _74173_3_pin6, driver_4_out, 1'b0, 1'b0, 1'b0, 1'b0, 1'b0, 1'b0, 1'b0, 1'b0, 1'b1
  not not_9 (tri_state_buffer_3_p2, Manual_Mode);
  Arch_RAM arch_ram_1 (
    .A0(driver_1_out), .A1(driver_2_out), .A2(driver_3_out), .A3(driver_4_out), .EN(1'b1),
    .Q0(arch_ram_1_q0), .Q1(arch_ram_1_q1), .Q2(arch_ram_1_q2), .Q3(arch_ram_1_q3), .Q4(arch_ram_1_q4),
    .Q5(arch_ram_1_q5), .Q6(arch_ram_1_q6), .Q7(arch_ram_1_q7));
  _74173 _74173_4 (
    .pin1(1'b0), .pin2(1'b0), .pin3(_74173_2_pin14), .pin4(_74173_2_pin13), .pin5(_74173_2_pin12),
    .pin6(_74173_2_pin11), .pin7(_74173_1_pin7), .pin8(1'b0), .pin9(_74173_1_pin9), .pin10(_74173_1_pin9),
    .pin11(tri_state_buffer_1_p18), .pin12(tri_state_buffer_1_p16), .pin13(tri_state_buffer_1_p14),
    .pin14(tri_state_buffer_1_p12), .pin15(Clear_out), .pin16(1'b1));
  LED led_11 (.in(_74173_2_pin13));
  LED led_12 (.in(_74173_2_pin12));
  not not_10 (tri_state_buffer_2_p2, _74173_3_pin9);
  LED u__64 (.in(arch_ram_1_q6));
  LED u__128 (.in(arch_ram_1_q7));
  LED led_13 (.in(_74173_2_pin11));
  LED u__4 (.in(arch_ram_1_q2));
  LED u__8 (.in(arch_ram_1_q3));
  LED u__16 (.in(arch_ram_1_q4));
  LED u__32 (.in(arch_ram_1_q5));
  LED u__1 (.in(arch_ram_1_q0));
  LED u__2 (.in(arch_ram_1_q1));
  LED led_14 (.in(clk));
  Button P (.out(P_out));
  // SwitchDT switchdt_1: pin names not known; wires that end beside it: clk, P_out, switchdt_1_p3
  and and_1 (_74173_1_pin7, switchdt_1_p3, not_11_out);
  not not_11 (not_11_out, or_1_out);
  or or_1 (or_1_out, HLT, control_rom_1_hlt);
  or or_2 (or_2_out, MI, control_rom_1_mi);
  or or_3 (or_3_out, MO, control_rom_1_mo);
  or or_4 (or_4_out, II, control_rom_1_ii);
  or or_5 (or_5_out, IO, control_rom_1_io);
  or or_6 (or_6_out, AI, control_rom_1_ai);
  or or_7 (or_7_out, AO, control_rom_1_ao);
  or or_8 (or_8_out, \ΣO , \control_rom_1_σo );
  or or_9 (or_9_out, \ΣS , \control_rom_1_σs );
  or or_10 (or_10_out, BI, control_rom_1_bi);
  or or_11 (or_11_out, OI, control_rom_1_oi);
  or or_12 (or_12_out, CE, control_rom_1_ce);
  or or_13 (or_13_out, CO, control_rom_1_co);
  or or_14 (or_14_out, J, control_rom_1_j);
  // Tri_State_Buffer tri_state_buffer_4: pin names not known; wires that end beside it: 1'b0, 1'b0, 1'b0, 1'b0, _74173_1_pin6, _74173_1_pin5, _74173_1_pin4, _74173_1_pin3, 1'b0, 1'b1, 1'b0, 1'b0, 1'b0, 1'b0, tri_state_buffer_1_p9, tri_state_buffer_1_p7, tri_state_buffer_1_p5, tri_state_buffer_1_p3, or_5_out
  not not_12 (_74173_3_pin9, or_2_out);
  // Tri_State_Buffer tri_state_buffer_5: pin names not known; wires that end beside it: arch_ram_1_q7, arch_ram_1_q6, arch_ram_1_q5, arch_ram_1_q4, arch_ram_1_q3, arch_ram_1_q2, arch_ram_1_q1, arch_ram_1_q0, 1'b0, 1'b1, tri_state_buffer_1_p17, tri_state_buffer_1_p15, tri_state_buffer_1_p13, tri_state_buffer_1_p11, tri_state_buffer_1_p9, tri_state_buffer_1_p7, tri_state_buffer_1_p5, tri_state_buffer_1_p3, or_3_out
  assign tri_state_buffer_1_p3 = in_10 ? _1 : 1'bz;  // Driver driver_5
  assign tri_state_buffer_1_p5 = in_10 ? _2 : 1'bz;  // Driver driver_6
  assign tri_state_buffer_1_p7 = in_10 ? _4 : 1'bz;  // Driver driver_7
  assign tri_state_buffer_1_p9 = in_10 ? _8 : 1'bz;  // Driver driver_8
  assign tri_state_buffer_1_p11 = in_10 ? _16 : 1'bz;  // Driver driver_9
  assign tri_state_buffer_1_p13 = in_10 ? _32 : 1'bz;  // Driver driver_10
  assign tri_state_buffer_1_p15 = in_10 ? _64 : 1'bz;  // Driver driver_11
  assign tri_state_buffer_1_p17 = in_10 ? _128 : 1'bz;  // Driver driver_12
  not not_13 (_74173_1_pin9, or_4_out);
  LED _128_2 (.in(tri_state_buffer_1_p17));
  LED _64_2 (.in(tri_state_buffer_1_p15));
  LED _32_2 (.in(tri_state_buffer_1_p13));
  LED _16_2 (.in(tri_state_buffer_1_p11));
  LED _8_2 (.in(tri_state_buffer_1_p9));
  LED _4_2 (.in(tri_state_buffer_1_p7));
  LED _2_2 (.in(tri_state_buffer_1_p5));
  LED _1_2 (.in(tri_state_buffer_1_p3));
  // Tri_State_Buffer tri_state_buffer_6: pin names not known; wires that end beside it: 1'b0, or_11_out, tri_state_buffer_1_p3, tri_state_buffer_6_p4, tri_state_buffer_1_p5, tri_state_buffer_6_p6, tri_state_buffer_1_p7, tri_state_buffer_6_p8, tri_state_buffer_1_p9, tri_state_buffer_6_p10, tri_state_buffer_1_p11, tri_state_buffer_6_p12, tri_state_buffer_1_p13, tri_state_buffer_6_p14, tri_state_buffer_1_p15, tri_state_buffer_6_p16, tri_state_buffer_1_p17, tri_state_buffer_6_p18, 1'b1
  not not_14 (not_14_out, or_11_out);
  _74173 _74173_5 (
    .pin1(1'b0), .pin2(1'b0), .pin3(_74173_5_pin3), .pin4(_74173_5_pin4), .pin5(_74173_5_pin5),
    .pin6(_74173_5_pin6), .pin7(_74173_1_pin7), .pin8(1'b0), .pin9(not_14_out), .pin10(not_14_out),
    .pin11(tri_state_buffer_6_p10), .pin12(tri_state_buffer_6_p8), .pin13(tri_state_buffer_6_p6),
    .pin14(tri_state_buffer_6_p4), .pin15(_74173_5_pin15), .pin16(1'b1));
  // Tri_State_Buffer tri_state_buffer_7: pin names not known; wires that end beside it: or_13_out, tri_state_buffer_1_p3, tri_state_buffer_1_p5, tri_state_buffer_1_p7, tri_state_buffer_1_p9, 1'b0, 1'b0, 1'b0, 1'b0, 1'b1, 1'b0, tri_state_buffer_7_p12, tri_state_buffer_7_p13, tri_state_buffer_7_p14, tri_state_buffer_7_p15, 1'b0, 1'b0, 1'b0, 1'b0
  // Tri_State_Buffer tri_state_buffer_8: pin names not known; wires that end beside it: or_7_out, tri_state_buffer_1_p3, tri_state_buffer_1_p5, tri_state_buffer_1_p7, tri_state_buffer_1_p9, tri_state_buffer_1_p11, tri_state_buffer_1_p13, tri_state_buffer_1_p15, tri_state_buffer_1_p17, 1'b1, 1'b0, tri_state_buffer_8_p12, tri_state_buffer_8_p13, tri_state_buffer_8_p14, tri_state_buffer_8_p15, tri_state_buffer_8_p16, tri_state_buffer_8_p17, tri_state_buffer_8_p18, tri_state_buffer_8_p19
  // Tri_State_Buffer tri_state_buffer_9: pin names not known; wires that end beside it: or_8_out, tri_state_buffer_1_p3, tri_state_buffer_1_p5, tri_state_buffer_1_p7, tri_state_buffer_1_p9, tri_state_buffer_1_p11, tri_state_buffer_1_p13, tri_state_buffer_1_p15, tri_state_buffer_1_p17, 1'b1, 1'b0, tri_state_buffer_9_p12, tri_state_buffer_9_p13, tri_state_buffer_9_p14, tri_state_buffer_9_p15, tri_state_buffer_9_p16, tri_state_buffer_9_p17, tri_state_buffer_9_p18, tri_state_buffer_9_p19
  // Tri_State_Buffer tri_state_buffer_10: pin names not known; wires that end beside it: 1'b0, tri_state_buffer_1_p3, tri_state_buffer_1_p5, tri_state_buffer_1_p7, tri_state_buffer_1_p9, tri_state_buffer_1_p11, tri_state_buffer_1_p13, tri_state_buffer_1_p15, tri_state_buffer_1_p17, 1'b1, 1'b0, tri_state_buffer_10_p12, tri_state_buffer_10_p13, tri_state_buffer_10_p14, tri_state_buffer_10_p15, tri_state_buffer_10_p16, tri_state_buffer_10_p17, tri_state_buffer_10_p18, tri_state_buffer_10_p19
  _74161 _74161_2 (
    .pin1(_74161_2_pin1), .pin2(_74173_1_pin7), .pin3(_74161_2_pin3), .pin4(_74161_2_pin4),
    .pin5(_74161_2_pin5), .pin6(_74161_2_pin6), .pin7(1'b1), .pin8(1'b0), .pin9(_74161_2_pin9),
    .pin10(or_12_out), .pin11(tri_state_buffer_7_p15), .pin12(tri_state_buffer_7_p14),
    .pin13(tri_state_buffer_7_p13), .pin14(tri_state_buffer_7_p12), .pin15(_74161_2_pin15), .pin16(1'b1));
  // Tri_State_Buffer tri_state_buffer_11: pin names not known; wires that end beside it: 1'b0, 1'b0, 1'b0, 1'b0, tri_state_buffer_1_p9, tri_state_buffer_1_p7, tri_state_buffer_1_p5, tri_state_buffer_1_p3, 1'b0, 1'b1, 1'b0, 1'b0, 1'b0, 1'b0, _74161_2_pin6, _74161_2_pin5, _74161_2_pin4, _74161_2_pin3, or_14_out
  // Tri_State_Buffer tri_state_buffer_12: pin names not known; wires that end beside it: tri_state_buffer_1_p17, tri_state_buffer_1_p15, tri_state_buffer_1_p13, tri_state_buffer_1_p11, tri_state_buffer_1_p9, tri_state_buffer_1_p7, tri_state_buffer_1_p5, tri_state_buffer_1_p3, 1'b0, 1'b1, tri_state_buffer_12_p11, tri_state_buffer_12_p12, tri_state_buffer_12_p13, tri_state_buffer_12_p14, tri_state_buffer_12_p15, tri_state_buffer_12_p16, tri_state_buffer_12_p17, tri_state_buffer_12_p18, or_6_out
  // Tri_State_Buffer tri_state_buffer_13: pin names not known; wires that end beside it: tri_state_buffer_1_p17, tri_state_buffer_1_p15, tri_state_buffer_1_p13, tri_state_buffer_1_p11, tri_state_buffer_1_p9, tri_state_buffer_1_p7, tri_state_buffer_1_p5, tri_state_buffer_1_p3, 1'b0, 1'b1, tri_state_buffer_13_p11, tri_state_buffer_13_p12, tri_state_buffer_13_p13, tri_state_buffer_13_p14, tri_state_buffer_13_p15, tri_state_buffer_13_p16, tri_state_buffer_13_p17, tri_state_buffer_13_p18, or_10_out
  LED _1_3 (.in(tri_state_buffer_7_p12));
  LED _2_3 (.in(tri_state_buffer_7_p13));
  LED _4_3 (.in(tri_state_buffer_7_p14));
  LED _8_3 (.in(tri_state_buffer_7_p15));
  LED led_15 (.in(_74161_2_pin15));
  not not_15 (not_15_out, or_6_out);
  _74173 _74173_6 (
    .pin1(1'b0), .pin2(1'b0), .pin3(tri_state_buffer_8_p12), .pin4(tri_state_buffer_8_p13),
    .pin5(tri_state_buffer_8_p14), .pin6(tri_state_buffer_8_p15), .pin7(_74173_1_pin7), .pin8(1'b0),
    .pin9(not_15_out), .pin10(not_15_out), .pin11(tri_state_buffer_12_p15), .pin12(tri_state_buffer_12_p16),
    .pin13(tri_state_buffer_12_p17), .pin14(tri_state_buffer_12_p18), .pin15(_74173_6_pin15), .pin16(1'b1));
  not not_16 (not_16_out, or_10_out);
  _74173 _74173_7 (
    .pin1(1'b0), .pin2(1'b0), .pin3(_74173_7_pin3), .pin4(_74173_7_pin4), .pin5(_74173_7_pin5),
    .pin6(_74173_7_pin6), .pin7(_74173_1_pin7), .pin8(1'b0), .pin9(not_14_out), .pin10(not_14_out),
    .pin11(tri_state_buffer_6_p18), .pin12(tri_state_buffer_6_p16), .pin13(tri_state_buffer_6_p14),
    .pin14(tri_state_buffer_6_p12), .pin15(_74173_5_pin15), .pin16(1'b1));
  not not_17 (_74161_2_pin9, or_14_out);
  Subtractor_Chip subtractor_chip_1 (
    .D0(tri_state_buffer_10_p12), .D1(tri_state_buffer_10_p13), .D2(tri_state_buffer_10_p14),
    .D3(tri_state_buffer_10_p15), .D4(tri_state_buffer_10_p16), .D5(tri_state_buffer_10_p17),
    .D6(tri_state_buffer_10_p18), .D7(tri_state_buffer_10_p19), .EN(or_9_out), .Q0(subtractor_chip_1_q0),
    .Q1(subtractor_chip_1_q1), .Q2(subtractor_chip_1_q2), .Q3(subtractor_chip_1_q3),
    .Q4(subtractor_chip_1_q4), .Q5(subtractor_chip_1_q5), .Q6(subtractor_chip_1_q6),
    .Q7(subtractor_chip_1_q7), .C0(subtractor_chip_1_c0));
  _74173 _74173_8 (
    .pin1(1'b0), .pin2(1'b0), .pin3(tri_state_buffer_8_p16), .pin4(tri_state_buffer_8_p17),
    .pin5(tri_state_buffer_8_p18), .pin6(tri_state_buffer_8_p19), .pin7(_74173_1_pin7), .pin8(1'b0),
    .pin9(not_15_out), .pin10(not_15_out), .pin11(tri_state_buffer_12_p11), .pin12(tri_state_buffer_12_p12),
    .pin13(tri_state_buffer_12_p13), .pin14(tri_state_buffer_12_p14), .pin15(_74173_6_pin15), .pin16(1'b1));
  _74173 _74173_9 (
    .pin1(1'b0), .pin2(1'b0), .pin3(tri_state_buffer_10_p16), .pin4(tri_state_buffer_10_p17),
    .pin5(tri_state_buffer_10_p18), .pin6(tri_state_buffer_10_p19), .pin7(_74173_1_pin7), .pin8(1'b0),
    .pin9(not_16_out), .pin10(not_16_out), .pin11(tri_state_buffer_13_p11), .pin12(tri_state_buffer_13_p12),
    .pin13(tri_state_buffer_13_p13), .pin14(tri_state_buffer_13_p14), .pin15(_74173_9_pin15), .pin16(1'b1));
  Button Clear_3 (.out(_74173_5_pin15));
  BIN_DEC_ONES_Decoder bin_dec_ones_decoder_1 (
    .a0(_74173_5_pin3), .EN(1'b1), .a1(_74173_5_pin4), .a2(_74173_5_pin5), .a3(_74173_5_pin6),
    .a4(_74173_7_pin3), .a5(_74173_7_pin4), .a6(_74173_7_pin5), .a7(_74173_7_pin6),
    .g(bin_dec_ones_decoder_1_g), .f(bin_dec_ones_decoder_1_f), .e(bin_dec_ones_decoder_1_e),
    .d(bin_dec_ones_decoder_1_d), .c(bin_dec_ones_decoder_1_c), .b(bin_dec_ones_decoder_1_b),
    .a(bin_dec_ones_decoder_1_a));
  BIN_DEC_TENS_Decoder bin_dec_tens_decoder_1 (
    .a0(_74173_5_pin3), .EN(1'b1), .a1(_74173_5_pin4), .a2(_74173_5_pin5), .a3(_74173_5_pin6),
    .a4(_74173_7_pin3), .a5(_74173_7_pin4), .a6(_74173_7_pin5), .a7(_74173_7_pin6),
    .g(bin_dec_tens_decoder_1_g), .f(bin_dec_tens_decoder_1_f), .e(bin_dec_tens_decoder_1_e),
    .d(bin_dec_tens_decoder_1_d), .c(bin_dec_tens_decoder_1_c), .b(bin_dec_tens_decoder_1_b),
    .a(bin_dec_tens_decoder_1_a));
  BIN_DEC_HUND_Decoder bin_dec_hund_decoder_1 (
    .a0(_74173_5_pin3), .EN(1'b1), .a1(_74173_5_pin4), .a2(_74173_5_pin5), .a3(_74173_5_pin6),
    .a4(_74173_7_pin3), .a5(_74173_7_pin4), .a6(_74173_7_pin5), .a7(_74173_7_pin6),
    .g(bin_dec_hund_decoder_1_g), .f(bin_dec_hund_decoder_1_f), .e(bin_dec_hund_decoder_1_e),
    .d(bin_dec_hund_decoder_1_d), .c(bin_dec_hund_decoder_1_c), .b(bin_dec_hund_decoder_1_b),
    .a(bin_dec_hund_decoder_1_a));
  Button Clear_4 (.out(Clear_4_out));
  not not_18 (_74161_2_pin1, Clear_4_out);
  Seven_Seg seven_seg_1 (
    .a(bin_dec_hund_decoder_1_a), .b(bin_dec_hund_decoder_1_b), .c(bin_dec_hund_decoder_1_c),
    .d(bin_dec_hund_decoder_1_d), .e(bin_dec_hund_decoder_1_e), .f(bin_dec_hund_decoder_1_f),
    .g(bin_dec_hund_decoder_1_g), .dp(1'b0));
  ALU_Arch alu_arch_1 (
    .B0(subtractor_chip_1_q0), .B1(subtractor_chip_1_q1), .B2(subtractor_chip_1_q2),
    .B3(subtractor_chip_1_q3), .B4(subtractor_chip_1_q4), .B5(subtractor_chip_1_q5),
    .B6(subtractor_chip_1_q6), .B7(subtractor_chip_1_q7), .C0(subtractor_chip_1_c0), .C1(alu_arch_1_c2),
    .A0(tri_state_buffer_8_p12), .A1(tri_state_buffer_8_p13), .A4(tri_state_buffer_8_p16),
    .A5(tri_state_buffer_8_p17), .A3(tri_state_buffer_8_p15), .A2(tri_state_buffer_8_p14),
    .A7(tri_state_buffer_8_p19), .A6(tri_state_buffer_8_p18), .C2(alu_arch_1_c2),
    .S3(tri_state_buffer_9_p15), .S7(tri_state_buffer_9_p19), .S6(tri_state_buffer_9_p18),
    .S4(tri_state_buffer_9_p16), .S1(tri_state_buffer_9_p13), .S0(tri_state_buffer_9_p12),
    .S5(tri_state_buffer_9_p17), .S2(tri_state_buffer_9_p14));  // open: C3
  Seven_Seg seven_seg_2 (
    .a(bin_dec_tens_decoder_1_a), .b(bin_dec_tens_decoder_1_b), .c(bin_dec_tens_decoder_1_c),
    .d(bin_dec_tens_decoder_1_d), .e(bin_dec_tens_decoder_1_e), .f(bin_dec_tens_decoder_1_f),
    .g(bin_dec_tens_decoder_1_g), .dp(1'b0));
  _74173 _74173_10 (
    .pin1(1'b0), .pin2(1'b0), .pin3(tri_state_buffer_10_p12), .pin4(tri_state_buffer_10_p13),
    .pin5(tri_state_buffer_10_p14), .pin6(tri_state_buffer_10_p15), .pin7(_74173_1_pin7), .pin8(1'b0),
    .pin9(not_16_out), .pin10(not_16_out), .pin11(tri_state_buffer_13_p15), .pin12(tri_state_buffer_13_p16),
    .pin13(tri_state_buffer_13_p17), .pin14(tri_state_buffer_13_p18), .pin15(_74173_9_pin15), .pin16(1'b1));
  Seven_Seg seven_seg_3 (
    .a(bin_dec_ones_decoder_1_a), .b(bin_dec_ones_decoder_1_b), .c(bin_dec_ones_decoder_1_c),
    .d(bin_dec_ones_decoder_1_d), .e(bin_dec_ones_decoder_1_e), .f(bin_dec_ones_decoder_1_f),
    .g(bin_dec_ones_decoder_1_g), .dp(1'b0));
  Button Clear_5 (.out(_74173_6_pin15));
  LED _1_4 (.in(tri_state_buffer_8_p12));
  LED _2_4 (.in(tri_state_buffer_8_p13));
  LED _4_4 (.in(tri_state_buffer_8_p14));
  LED _8_4 (.in(tri_state_buffer_8_p15));
  LED _16_3 (.in(tri_state_buffer_8_p16));
  LED _32_3 (.in(tri_state_buffer_8_p17));
  LED _64_3 (.in(tri_state_buffer_8_p18));
  LED _128_3 (.in(tri_state_buffer_8_p19));
  LED _1_5 (.in(tri_state_buffer_10_p12));
  LED _2_5 (.in(tri_state_buffer_10_p13));
  LED _4_5 (.in(tri_state_buffer_10_p14));
  LED _8_5 (.in(tri_state_buffer_10_p15));
  LED _16_4 (.in(tri_state_buffer_10_p16));
  LED _32_4 (.in(tri_state_buffer_10_p17));
  LED _64_4 (.in(tri_state_buffer_10_p18));
  LED _128_4 (.in(tri_state_buffer_10_p19));
  Button Clear_6 (.out(_74173_9_pin15));

  // Notes on the sheet:
  //   clk: Hz: 5
  //   Control Logic
  //   Step Counter
  //   Memory Set
  //   R:I
  //   Addr. Bits
  //   MAR
  //   64 Bit Memory
  //   Instr. Bits
  //   5hz Clock
  //   Byte Loader
  //   HLT
  //   MI
  //   MO
  //   II
  //   IO
  //   AI
  //   AO
  //   ΣO
  //   ΣS
  //   BI
  //   OI
  //   CE
  //   CO
  //   J
  //   MAIN BUS
  //   Logic Bus
  //   PC
  //   R:A
  //   ALU
  //   R:B
endmodule
