// Digital circuit BIN_DEC_TENS_Decoder.dig as structural Verilog
module BIN_DEC_TENS_Decoder (
  input  a0,
  input  EN,
  input  a1,
  input  a2,
  input  a3,
  input  a4,
  input  a5,
  input  a6,
  input  a7,
  output g,
  output f,
  output e,
  output d,
  output c,
  output b,
  output a
);

  ROM #(.AddrBits(8), .Bits(7)) rom_1 (.A({a7, a6, a5, a4, a3, a2, a1, a0}), .sel(EN), .D({a, b, c, d, e, f, g}));

  // Notes on the sheet:
  //   contents of rom_1 (hex, n*v repeats v):
  //   10*7e,10*30,10*6d,10*79,10*33,10*5b,10*5f,10*70,10*7f,10*7b,10*7e
  //   ,10*30,10*6d,10*79,10*33,10*5b,10*5f,10*70,10*7f,10*7b,10*7e,10*30
  //   ,10*6d,10*79,10*33,6*5b
endmodule
