// Digital circuit Bus Transceiver.dig as structural Verilog
module Bus_Transceiver (
  input  VCC,
  input  GND,
  input  D0,
  input  D1,
  input  D2,
  input  D3,
  input  D4,
  input  D5,
  input  D6,
  input  D7,
  input  CE,
  output O0,
  output O1,
  output O2,
  output O3,
  output O4,
  output O5,
  output O6,
  output O7
);

  PowerSupply powersupply_1 (.VDD(VCC), .GND(GND));
  assign O0 = CE ? D0 : 1'bz;  // Driver driver_1
  assign O1 = CE ? D1 : 1'bz;  // Driver driver_2
  assign O2 = CE ? D2 : 1'bz;  // Driver driver_3
  assign O3 = CE ? D3 : 1'bz;  // Driver driver_4
  assign O4 = CE ? D4 : 1'bz;  // Driver driver_5
  assign O5 = CE ? D5 : 1'bz;  // Driver driver_6
  assign O6 = CE ? D6 : 1'bz;  // Driver driver_7
  assign O7 = CE ? D7 : 1'bz;  // Driver driver_8

  // Notes on the sheet:
  //   VCC: pin 10, default 1
  //   GND: pin 20
  //   D0: pin 19
  //   D1: pin 18
  //   D2: pin 17
  //   D3: pin 16
  //   D4: pin 15
  //   D5: pin 14
  //   D6: pin 13
  //   D7: pin 12
  //   CE: pin 1
  //   O0: pin 2
  //   O1: pin 3
  //   O2: pin 4
  //   O3: pin 5
  //   O4: pin 6
  //   O5: pin 7
  //   O6: pin 8
  //   O7: pin 9
endmodule
