// Digital circuit Control_Rom.dig as structural Verilog
module Control_Rom (
  input  S0,
  input  S1,
  input  S2,
  input  I0,
  input  I1,
  input  I2,
  input  I3,
  input  EN,
  output J,
  output CO,
  output CE,
  output OI,
  output BI,
  output \ΣS ,
  output \ΣO ,
  output AO,
  output AI,
  output IO,
  output II,
  output MO,
  output MI,
  output HLT
);

  ROM #(.AddrBits(7), .Bits(14)) rom_1 (
    .A({I3, I2, I1, I0, S2, S1, S0}), .sel(EN),
    .D({HLT, MI, MO, II, IO, AI, AO, \ΣO , \ΣS , BI, OI, CE, CO, J}));

  // Notes on the sheet:
  //   contents of rom_1 (hex, n*v repeats v):
  //   0,0,0,1002,c04,0,0,0,1200,900,0,1002,c04,0,0,0,1200,810,140,1002
  //   ,c04,0,0,0,88,0,0,1002,c04,6*0,1002,c04,6*0,1002,c04,6*0,1002
  //   ,c04,6*0,1002,c04,0,0,0,2000,0,0,1002,c04,6*0,1002,c04,6*0,1002
  //   ,c04,6*0,1002,c04,6*0,1002,c04,6*0,1002,c04,6*0,1002,c04,6*0,1002,c04
endmodule
