// Digital circuit Register_Arch.dig as structural Verilog
module Register_Arch (
  input  D0,
  input  D1,
  input  D2,
  input  D3,
  input  D4,
  input  D5,
  input  D6,
  input  D7,
  input  DE,
  input  CLK,
  input  QE,
  output Q0,
  output Q1,
  output Q2,
  output Q3,
  output Q4,
  output Q5,
  output Q6,
  output Q7
);

  wire _74173_1_pin3, _74173_1_pin4, _74173_1_pin5, _74173_1_pin6, _74173_1_pin9, _74173_2_pin3,
       _74173_2_pin4, _74173_2_pin5, _74173_2_pin6;

  _74173 _74173_1 (
    .pin1(1'b0), .pin2(1'b0), .pin3(_74173_1_pin3), .pin4(_74173_1_pin4), .pin5(_74173_1_pin5),
    .pin6(_74173_1_pin6), .pin7(CLK), .pin8(1'b0), .pin9(_74173_1_pin9), .pin10(_74173_1_pin9), .pin11(D3),
    .pin12(D2), .pin13(D1), .pin14(D0), .pin15(1'b0), .pin16(1'b1));
  Bus_Transceiver bus_transceiver_1 (
    .VCC(1'b1), .GND(1'b0), .D0(_74173_1_pin3), .D1(_74173_1_pin4), .D2(_74173_1_pin5), .D3(_74173_1_pin6),
    .D4(_74173_2_pin3), .D5(_74173_2_pin4), .D6(_74173_2_pin5), .D7(_74173_2_pin6), .CE(QE), .O0(Q0),
    .O1(Q1), .O2(Q2), .O3(Q3), .O4(Q4), .O5(Q5), .O6(Q6), .O7(Q7));
  _74173 _74173_2 (
    .pin1(1'b0), .pin2(1'b0), .pin3(_74173_2_pin3), .pin4(_74173_2_pin4), .pin5(_74173_2_pin5),
    .pin6(_74173_2_pin6), .pin7(CLK), .pin8(1'b0), .pin9(_74173_1_pin9), .pin10(_74173_1_pin9), .pin11(D7),
    .pin12(D6), .pin13(D5), .pin14(D4), .pin15(1'b0), .pin16(1'b1));
  not not_1 (_74173_1_pin9, DE);

  // Notes on the sheet:
  //   D0: pin 3
  //   D1: pin 4
  //   D2: pin 5
  //   D3: pin 6
  //   D4: pin 7
  //   D5: pin 8
  //   D6: pin 9
  //   D7: pin 10
  //   DE: pin 2
  //   Q0: pin 18
  //   Q1: pin 17
  //   Q2: pin 16
  //   Q3: pin 15
  //   Q4: pin 14
  //   Q5: pin 13
  //   Q6: pin 12
  //   Q7: pin 11
  //   CLK: pin 20
  //   QE: pin 19
  //   A
endmodule
