// Digital circuit Subtractor_Chip.dig as structural Verilog
module Subtractor_Chip (
  input  D0,
  input  D1,
  input  D2,
  input  D3,
  input  D4,
  input  D5,
  input  D6,
  input  D7,
  input  EN,
  output Q0,
  output Q1,
  output Q2,
  output Q3,
  output Q4,
  output Q5,
  output Q6,
  output Q7,
  output C0
);

  xor xor_1 (Q0, D0, EN);
  xor xor_2 (Q1, D1, EN);
  xor xor_3 (Q2, D2, EN);
  xor xor_4 (Q3, D3, EN);
  xor xor_5 (Q4, D4, EN);
  xor xor_6 (Q5, D5, EN);
  xor xor_7 (Q6, D6, EN);
  xor xor_8 (Q7, D7, EN);

  assign C0 = EN;

  // Notes on the sheet:
  //   D0: pin 8
  //   D1: pin 7
  //   D2: pin 6
  //   D3: pin 5
  //   D4: pin 4
  //   D5: pin 3
  //   D6: pin 2
  //   D7: pin 1
  //   EN: pin 10
  //   Q0: pin 11
  //   Q1: pin 12
  //   Q2: pin 13
  //   Q3: pin 14
  //   Q4: pin 15
  //   Q5: pin 16
  //   Q6: pin 17
  //   Q7: pin 18
  //   C0: pin 9
endmodule
